# Fritzing sketch Circuit DHT22 (saved by Fritzing 0.9.3b)
circuit board: 8.46667cm x 5.64444cm
breadboards: 1

parts:
  R1 = Resistor [tolerance=±5% resistance=4.7k package=THT]
  DHT22 = Humidity and Temperature Sensor RHT03
  Arduino_Uno = Arduino Uno (Rev3)

nets:
  VCC: R1.Pin_0, DHT22.Vcc, Arduino_Uno.3V3
  N1: R1.Pin_1, DHT22.Data-signal, Arduino_Uno.D2
  N2: DHT22.GND_2, Arduino_Uno.GND

// code stored in the sketch: DHT22.ino
//--------------------------------------------
//        Test complet du capteur DHT22
// 
// EG - 04.02.17
// Version : 2.0
//-------------------------------------------
// 
//-------------------------------------------
// Attention fonctionnement en 3.3V

//Inclusion des librairies récentes
#include <Adafruit_Sensor.h>
#include <DHT.h>
#include <DHT_U.h>
//Sources : https://github.com/adafruit/DHT-sensor-library

//Déclaration des constantes

//
#define DHTPIN 2     // déclaration de l'input utilisé sur la carte Arduino
#define DHTTYPE DHT22   // Déclaration du type de capteur DHTxx

// Initialisation du capteur DHT22
//DHT dht(DHTPIN, DHTTYPE);

DHT_Unified dht(DHTPIN, DHTTYPE);

//Initialisation
void setup() {
  //Ouverture du port Série à 9600 Baud
  Serial.begin(9600);
  //Envoi du texte de démarrage
  Serial.println("Lancement du test DHT22");
  //Démarrage du capteur DHT22
  dht.begin();
  pinMode(LED_BUILTIN, OUTPUT);
  //Attente avant première mesure
  delay(2000);

    // Print temperature sensor details.
  sensor_t sensor;
  dht.temperature().getSensor(&sensor);
}

//Boucle de fonctionnement
void loop() {

digitalWrite(LED_BUILTIN, LOW);

  // Reading temperature or humidity takes about 250 milliseconds!
  // Lecture du taux d'humidity en %
  float h = dht.readHumidity();
  // Lecture de la température en dégré Celsius
  float t = dht.readTemperature();


  // Check if any reads failed and exit early (to try again).
  if (isnan(h) || isnan(t)) {
    Serial.println("Impossible de lire le capteur DHT22 !");
    return;
  }


  // Compute heat index in Celsius (isFahreheit = false)
  //float hic = dht.computeHeatIndex(t, h, false);

  Serial.print("Hum.: ");
  Serial.print(h);
  Serial.print("%\t");
  Serial.print("Temp.: ");
  Serial.print(t);
  Serial.println(" °C");
  
  //Attente entre 2 mesures d'une seconde
  delay(1000);
}
