# Fritzing sketch Circuit ILS (saved by Fritzing 0.9.3b)
breadboards: 1

parts:
  Reed_Switch_-_LM393 = mystery part, 3 pins [chip_label=ILS]
  Composant1 = Arduino Uno (Rev3)

nets:
  N1: Reed_Switch_-_LM393.pin1, Composant1.D8
  N2: Reed_Switch_-_LM393.pin2, Composant1.GND
  N3: Reed_Switch_-_LM393.pin3, Composant1.3V3
